// Logisim project 4Bit_ALU.circ as structural Verilog: 8 circuits, main circuit main
module main (
  input  in_1,
  input  [3:0] in_2,
  input  in_3,
  input  in_4,
  input  in_5,
  input  in_6,
  input  [3:0] in_7,
  output [3:0] out_8,
  output Overflow,
  output Carry
);

  wire [3:0] n4_bit_lu_1_y, n4bitau_1_out_7;

  _4_bit_LU u_4_bit_lu_1 (.S1(in_6), .S0(in_5), .B(in_2), .in_4(in_7), .Y(n4_bit_lu_1_y));
  _4bitAU u_4bitau_1 (
    .Cin(in_1), .in_2(in_2), .in_3(in_7), .in_4(in_3), .S1(in_5), .S0(in_6), .out_7(n4bitau_1_out_7),
    .out_8(Overflow), .out_9(Carry));
  _4_bit_2x1_MUX u_4_bit_2x1_mux_1 (.in_1(n4bitau_1_out_7), .in_2(n4_bit_lu_1_y), .in_3(in_4), .out_4(out_8));
endmodule

module full_adder (
  input  in_1,
  input  in_2,
  input  in_3,
  output out_4,
  output out_5
);

  wire and_1_out, and_2_out, xor_1_out;

  xor xor_1 (xor_1_out, in_2, in_3);
  and and_1 (and_1_out, in_1, xor_1_out);
  and and_2 (and_2_out, in_3, in_2);
  xor xor_2 (out_4, xor_1_out, in_1);
  or or_1 (out_5, and_1_out, and_2_out);
endmodule

module _4x1_MUX (
  input  in_1,
  input  in_2,
  input  in_3,
  input  in_4,
  input  in_5,
  input  in_6,
  output out_7
);

  wire and_1_out, and_2_out, and_3_out, and_4_out, not_1_out, not_2_out;

  not not_1 (not_1_out, in_1);
  not not_2 (not_2_out, in_2);
  and and_1 (and_1_out, in_3, in_2, in_2);
  and and_2 (and_2_out, in_4, not_1_out, in_2);
  and and_3 (and_3_out, in_5, not_2_out, in_2);
  and and_4 (and_4_out, in_6, not_1_out, not_2_out);
  or or_1 (out_7, and_1_out, and_2_out, and_3_out, and_4_out);
endmodule

module _4bitAU (
  input  Cin,
  input  [3:0] in_2,
  input  [3:0] in_3,
  input  in_4,
  input  S1,
  input  S0,
  output [3:0] out_7,
  output out_8,
  output out_9
);

  wire full_adder_1_out_5, full_adder_2_out_5, full_adder_3_out_5, n4x1_mux_1_out_7, n4x1_mux_2_out_7,
       n4x1_mux_3_out_7, n4x1_mux_4_out_7, not_1_out, not_2_out, not_3_out, not_4_out, not_5_out;

  not not_1 (not_1_out, in_4);
  not not_2 (not_2_out, in_3[0]);
  not not_3 (not_3_out, in_3[1]);
  not not_4 (not_4_out, in_3[2]);
  not not_5 (not_5_out, in_3[3]);
  _4x1_MUX u_4x1_mux_1 (
    .in_1(S0), .in_2(S1), .in_3(in_3[0]), .in_4(not_2_out), .in_5(in_4), .in_6(not_1_out),
    .out_7(n4x1_mux_1_out_7));
  _4x1_MUX u_4x1_mux_2 (
    .in_1(S0), .in_2(S1), .in_3(in_3[1]), .in_4(not_3_out), .in_5(in_4), .in_6(not_1_out),
    .out_7(n4x1_mux_2_out_7));
  _4x1_MUX u_4x1_mux_3 (
    .in_1(S0), .in_2(S1), .in_3(in_3[2]), .in_4(not_4_out), .in_5(in_4), .in_6(not_1_out),
    .out_7(n4x1_mux_3_out_7));
  _4x1_MUX u_4x1_mux_4 (
    .in_1(S0), .in_2(S1), .in_3(in_3[3]), .in_4(not_5_out), .in_5(in_4), .in_6(not_1_out),
    .out_7(n4x1_mux_4_out_7));
  full_adder full_adder_1 (
    .in_1(Cin), .in_2(in_2[0]), .in_3(n4x1_mux_1_out_7), .out_4(out_7[0]), .out_5(full_adder_1_out_5));
  full_adder full_adder_2 (
    .in_1(full_adder_1_out_5), .in_2(in_2[1]), .in_3(n4x1_mux_2_out_7), .out_4(out_7[1]),
    .out_5(full_adder_2_out_5));
  full_adder full_adder_3 (
    .in_1(full_adder_2_out_5), .in_2(in_2[2]), .in_3(n4x1_mux_3_out_7), .out_4(out_7[2]),
    .out_5(full_adder_3_out_5));
  full_adder full_adder_4 (
    .in_1(full_adder_3_out_5), .in_2(in_2[3]), .in_3(n4x1_mux_4_out_7), .out_4(out_7[3]), .out_5(out_9));
  xor xor_1 (out_8, full_adder_3_out_5, out_9);
endmodule

module _1_bit_lU (
  input  in_1,
  input  in_2,
  input  in_3,
  input  in_4,
  output out_5
);

  wire and_1_out, not_1_out, or_1_out, xor_1_out;

  not not_1 (not_1_out, in_1);
  and and_1 (and_1_out, in_1, in_2);
  or or_1 (or_1_out, in_1, in_2);
  xor xor_1 (xor_1_out, in_1, in_2);
  _4x1_MUX u_4x1_mux_1 (
    .in_1(in_3), .in_2(in_4), .in_3(and_1_out), .in_4(or_1_out), .in_5(xor_1_out), .in_6(not_1_out),
    .out_7(out_5));
endmodule

module _4_bit_LU (
  input  S1,
  input  S0,
  input  [3:0] B,
  input  [3:0] in_4,
  output [3:0] Y
);

  _1_bit_lU u_1_bit_lu_1 (.in_1(B[0]), .in_2(in_4[0]), .in_3(S0), .in_4(S1), .out_5(Y[0]));
  _1_bit_lU u_1_bit_lu_2 (.in_1(B[1]), .in_2(in_4[1]), .in_3(S0), .in_4(S1), .out_5(Y[1]));
  _1_bit_lU u_1_bit_lu_3 (.in_1(B[2]), .in_2(in_4[2]), .in_3(S0), .in_4(S1), .out_5(Y[2]));
  _1_bit_lU u_1_bit_lu_4 (.in_1(B[3]), .in_2(in_4[3]), .in_3(S0), .in_4(S1), .out_5(Y[3]));

  // Notes on the sheet:
  //   A
endmodule

module _1_bit_MUX (
  input  D0,
  input  D1,
  input  D2,
  output out_4
);

  wire nand_1_out, nand_2_out, nand_3_out;

  nand nand_1 (nand_1_out, D2, D2);
  nand nand_2 (nand_2_out, nand_1_out, D0);
  nand nand_3 (nand_3_out, D2, D1);
  nand nand_4 (out_4, nand_2_out, nand_3_out);
endmodule

module _4_bit_2x1_MUX (
  input  [3:0] in_1,
  input  [3:0] in_2,
  input  in_3,
  output [3:0] out_4
);

  _1_bit_MUX u_1_bit_mux_1 (.D0(in_1[0]), .D1(in_2[0]), .D2(in_3), .out_4(out_4[0]));
  _1_bit_MUX u_1_bit_mux_2 (.D0(in_1[1]), .D1(in_2[1]), .D2(in_3), .out_4(out_4[1]));
  _1_bit_MUX u_1_bit_mux_3 (.D0(in_1[2]), .D1(in_2[2]), .D2(in_3), .out_4(out_4[2]));
  _1_bit_MUX u_1_bit_mux_4 (.D0(in_1[3]), .D1(in_2[3]), .D2(in_3), .out_4(out_4[3]));
endmodule
