// Logisim project Adder.circ as structural Verilog: 1 circuit, main circuit main
module main (
  input  in_1,
  input  in_2,
  input  in_3,
  input  in_4,
  input  in_5,
  input  in_6,
  input  in_7,
  input  in_8,
  input  in_9,
  input  in_10,
  input  in_11,
  input  in_12,
  input  in_13,
  input  in_14,
  input  in_15,
  input  in_16,
  input  in_17,
  input  in_18
);

  wire and_1_out, and_2_out, and_3_out, and_4_out, and_5_out, and_6_out, and_7_out, and_8_out, and_9_out,
       and_10_out, and_11_out, and_12_out, and_13_out, and_14_out, and_15_out, and_16_out, and_17_out,
       and_18_out, and_19_out, and_20_out, and_21_out, and_22_out, not_1_out, not_2_out, not_3_out,
       not_4_out, not_5_out, not_6_out, not_7_out, not_8_out, not_9_out, not_10_out, not_11_out, not_12_out,
       not_13_out, not_14_out, not_15_out, not_16_out, not_17_out, not_18_out, not_19_out, not_20_out,
       not_21_out, not_22_out, not_23_out, not_24_out, or_1_out, or_2_out, or_3_out, xor_1_out, xor_2_out;

  buf and_1 (and_1_out, in_1);  // AND_Gate
  and and_2 (and_2_out, in_5, in_8);
  not not_1 (not_1_out, and_2_out);
  and and_3 (and_3_out, in_10, in_12);
  not not_2 (not_2_out, and_1_out);
  not not_3 (not_3_out, and_3_out);
  and and_4 (and_4_out, in_1, not_2_out);
  not not_4 (not_4_out, and_4_out);
  not not_5 (not_5_out, and_5_out);
  and and_5 (and_5_out, not_2_out, in_3);
  and and_6 (and_6_out, in_5, not_1_out);
  not not_6 (not_6_out, and_6_out);
  and and_7 (and_7_out, not_1_out, in_8);
  not not_7 (not_7_out, and_7_out);
  not not_8 (not_8_out, and_8_out);
  and and_8 (and_8_out, in_10, not_3_out);
  not not_9 (not_9_out, and_9_out);
  and and_9 (and_9_out, not_3_out, in_12);
  not not_10 (not_10_out, and_10_out);
  and and_10 (and_10_out, in_15, in_17);
  and and_11 (and_11_out, not_4_out, not_5_out);
  and and_12 (and_12_out, not_6_out, not_7_out);
  not not_11 (not_11_out, not_1_out);
  and and_13 (and_13_out, not_8_out, not_9_out);
  LED led_1 (.in(not_10_out));
  LED led_2 (.in(not_12_out));
  not not_12 (not_12_out, and_11_out);
  not not_13 (not_13_out, and_12_out);
  LED led_3 (.in(not_13_out));
  LED led_4 (.in(not_11_out));
  not not_14 (not_14_out, and_13_out);
  LED led_5 (.in(not_14_out));
  or or_1 (or_1_out, in_16, in_18);
  and and_14 (and_14_out, in_2, in_4);
  LED led_6 (.in(not_15_out));
  not not_15 (not_15_out, or_1_out);
  not not_16 (not_16_out, and_14_out);
  not not_17 (not_17_out, and_15_out);
  and and_15 (and_15_out, in_2, not_16_out);
  not not_18 (not_18_out, and_16_out);
  and and_16 (and_16_out, not_16_out, in_4);
  xor xor_1 (xor_1_out, in_6, in_7);
  and and_17 (and_17_out, in_7, in_6);
  not not_19 (not_19_out, in_11);
  and and_18 (and_18_out, not_17_out, not_18_out);
  not not_20 (not_20_out, and_18_out);
  and and_19 (and_19_out, in_9, xor_1_out);
  xor xor_2 (xor_2_out, xor_1_out, in_9);
  and and_20 (and_20_out, not_19_out, in_13, in_14);
  not not_21 (not_21_out, not_20_out);
  LED led_7 (.in(not_21_out));
  or or_2 (or_2_out, and_19_out, and_17_out);
  not not_22 (not_22_out, in_11);
  not not_23 (not_23_out, in_13);
  not not_24 (not_24_out, in_14);
  LED led_8 (.in(xor_2_out));
  LED led_9 (.in(or_2_out));
  and and_21 (and_21_out, not_22_out, not_23_out, not_24_out);
  and and_22 (and_22_out, in_11, not_23_out, in_14);
  LED led_10 (.in(or_3_out));
  or or_3 (or_3_out, and_20_out, and_21_out, and_22_out);

  // Notes on the sheet:
  //   XOR
  //   HALF ADDER
  //   NAND
  //   NOR
  //   XNOR
  //   FULL ADDER
  //   Y=A|BC+A|B|C|+AB|C
endmodule
