// Logisim project Subtractor.circ as structural Verilog: 1 circuit, main circuit main
module main (
  input  A,
  input  S,
  input  in_3,
  input  B,
  input  A_2,
  input  D,
  input  B_2,
  input  Bin,
  input  in_9
);

  wire and_1_out, and_2_out, and_3_out, not_1_out, not_2_out, not_3_out, or_1_out, xor_1_out, xor_2_out,
       xor_3_out;

  xor xor_1 (xor_1_out, A, in_3);
  not not_1 (not_1_out, A);
  and and_1 (and_1_out, not_1_out, in_3);
  xor xor_2 (xor_2_out, B_2, Bin);
  not not_2 (not_2_out, B_2);
  and and_2 (and_2_out, not_2_out, Bin);
  xor xor_3 (xor_3_out, A_2, xor_2_out);
  not not_3 (not_3_out, xor_2_out);
  and and_3 (and_3_out, not_3_out, A_2);
  or or_1 (or_1_out, and_3_out, and_2_out);

  // Notes on the sheet:
  //   B
  //   Bout
endmodule
