// Logisim project fullAdder_MUX.circ as structural Verilog: 1 circuit, main circuit main
module main (
  input  C,
  input  B,
  input  A,
  input  in_4,
  input  in_5,
  output out_6,
  output out_7
);

  wire not_1_out;

  not not_1 (not_1_out, C);
  // MUX_main main_1: pin names not known; wires that end beside it: B, A, C, not_1_out, not_1_out, C, out_6
  // MUX_main main_2: pin names not known; wires that end beside it: B, A, in_4, C, C, in_5, out_7
endmodule
