// Logisim project halfAdder_MUX.circ as structural Verilog: 1 circuit, main circuit main
module main (
  input  X,
  input  in_2,
  input  A3,
  input  A2,
  input  A1,
  input  A0,
  input  A3_2,
  input  A2_2,
  input  A1_2,
  input  A0_2,
  output S,
  output C
);

  // MUX_main main_1: pin names not known; wires that end beside it: X, in_2, A3, A2, A1, A0, S
  // MUX_main main_2: pin names not known; wires that end beside it: X, in_2, A3_2, A2_2, A1_2, A0_2, C

  // Notes on the sheet:
  //   Y
  //   Y
  //   X
endmodule
