// Logisim project read_write_register.circ as structural Verilog: 1 circuit, main circuit main
module main (
  input  in_1,
  input  [1:0] in_2,
  input  [1:0] in_3,
  input  in_4,
  input  [1:0] in_5,
  input  in_6,
  input  [3:0] in_7,
  output [3:0] out_8,
  output [3:0] out_9
);

  wire and_1_out, and_2_out, and_3_out, and_4_out, clock_1_out, clock_2_out, decoder_1_out0, decoder_1_out1,
       decoder_1_out2, decoder_1_out3;
  wire [3:0] register_1_q, register_2_q, register_3_q, register_4_q;

  Clock clock_1 (.out(clock_1_out));
  Decoder #(.select(2)) decoder_1 (
    .out0(decoder_1_out0), .out1(decoder_1_out1), .out2(decoder_1_out2), .out3(decoder_1_out3), .sel(in_3),
    .en(in_4));
  and and_1 (and_1_out, clock_1_out, decoder_1_out0);
  and and_2 (and_2_out, clock_1_out, decoder_1_out1);
  and and_3 (and_3_out, clock_1_out, decoder_1_out2);
  and and_4 (and_4_out, clock_1_out, decoder_1_out3);
  Clock clock_2 (.out(clock_2_out));
  Register #(.width(4)) register_1 (.D(in_7), .en(and_1_out), .Q(register_1_q), .clk(clock_2_out));  // open: clr
  Register #(.width(4)) register_2 (.D(in_7), .en(and_2_out), .Q(register_2_q), .clk(clock_2_out));  // open: clr
  Register #(.width(4)) register_3 (.D(in_7), .en(and_3_out), .Q(register_3_q), .clk(clock_2_out));  // open: clr
  Register #(.width(4)) register_4 (.D(in_7), .en(and_4_out), .Q(register_4_q), .clk(clock_2_out));  // open: clr
  Multiplexer #(.select(2), .width(4)) multiplexer_1 (
    .in0(register_1_q), .in1(register_2_q), .in2(register_3_q), .in3(register_4_q), .out(out_8), .sel(in_2),
    .en(in_1));
  Multiplexer #(.select(2), .width(4)) multiplexer_2 (
    .in0(register_1_q), .in1(register_2_q), .in2(register_3_q), .in3(register_4_q), .out(out_9), .sel(in_5),
    .en(in_6));
endmodule
